// Logisim project Farhan_2008060_Modified_SAP1.circ as structural Verilog: 29 circuits, main circuit alu
module main (
  input  in_1,
  input  in_2,
  output [7:0] out_3,
  output [7:0] out_4,
  output [7:0] out_5,
  output [7:0] out_6,
  output [7:0] out_7,
  output [7:0] out_8,
  output [7:0] out_9,
  output [7:0] out_10,
  output [7:0] out_11,
  output [7:0] out_12,
  output [7:0] out_13,
  output [7:0] out_14,
  output [7:0] out_15,
  output [7:0] out_16,
  output [7:0] out_17,
  output [7:0] out_18,
  output [7:0] out_19,
  output [3:0] hex,
  output [3:0] out_21,
  output [7:0] out_22
);

  wire a_in_en, a_out_en, alu_out_en, b_in_en, b_out_en, boot_loaded, clk, clk_out, debug, flag_in_en, hlt,
       ins_reg_in_en, ins_reg_out_en, mar_in_en, not_2_out, or_1_out, or_2_out, pc_in_en, pc_inc, pc_out_en,
       power, reset, sram_rd, sram_wr;
  wire [0:0] clk_counter_1_ex_bit;
  wire [3:0] clk_counter_1_count, control_seq_1_t_state, flag_in, flag_out, gp_reg_2_reg_int_out,
       gp_reg_2_reg_int_out_2, pc_1_pc_value;
  wire [7:0] control_word, debug_data, gp_reg_1_reg_int_out, rom_1_data, sram_addr;

  sram sram_1 (
    .sram_rd(sram_rd), .sram_wr(sram_wr), .sram_d_in(out_8), .mar_d_in(out_8), .mar_in_en(mar_in_en),
    .sram_clk(clk), .sram_clear(in_1), .sram_d_out(out_8), .Ox0(out_3), .Ox1(out_4), .Ox2(out_5),
    .Ox3(out_6), .Ox4(out_7), .Ox5(out_9), .Ox6(out_10), .Ox7(out_11), .Ox8(out_12), .Ox9(out_13),
    .OxA(out_14), .OxB(out_15), .OxC(out_16), .OxD(out_17), .OxE(out_18), .OxF(out_19));
  Hex_Digit_Display #(.decimalPoint("false")) hex_digit_display_1 (.value(out_8[3:0]));
  Hex_Digit_Display #(.decimalPoint("false")) hex_digit_display_2 (.value(out_8[7:4]));
  Hex_Digit_Display #(.decimalPoint("false")) hex_digit_display_3 (.value(pc_1_pc_value));
  pc pc_1 (
    .pc_inc(pc_inc), .pc_in_en(pc_in_en), .pc_in(hex), .clk(clk), .reset(in_2), .pc_out_en(pc_out_en),
    .pc_value(pc_1_pc_value), .pc_out(out_8[3:0]));  // open: c_out
  ROM #(.addrWidth(4)) rom_1 (.addr(sram_addr[3:0]), .data(rom_1_data));
  assign out_8 = debug ? debug_data : 8'bz;  // Controlled_Buffer controlled_buffer_1
  gp_reg gp_reg_1 (
    .reg_in(out_8), .reg_in_en(a_in_en), .reg_clk(clk), .reg_out_en(a_out_en), .reset(reset),
    .reg_int_out(gp_reg_1_reg_int_out), .reg_out(out_8));
  gp_reg gp_reg_2 (
    .reg_in(out_8), .reg_in_en(b_in_en), .reg_clk(clk), .reg_out_en(b_out_en), .reset(reset),
    .reg_int_out({gp_reg_2_reg_int_out_2, gp_reg_2_reg_int_out}), .reg_out(out_8));
  ins_reg ins_reg_1 (
    .ins_reg_in(out_8), .ins_reg_in_en(ins_reg_in_en), .clk(clk), .ins_reg_out_en(ins_reg_out_en),
    .operand_int(hex), .operand(out_8[3:0]), .opcode(out_21));
  bootloader bootloader_1 (
    .reset(reset), .en(debug), .clk(clk), .sram_data(rom_1_data), .debug_data(debug_data),
    .mar_in_en(mar_in_en), .sram_wr(sram_wr), .boot_loaded(boot_loaded), .sram_addr(sram_addr));
  LED led_1 (.in(flag_out[3]));
  LED led_2 (.in(flag_out[2]));
  LED led_3 (.in(flag_out[1]));
  Hex_Digit_Display #(.decimalPoint("false")) address (.value(hex));
  Hex_Digit_Display #(.decimalPoint("false")) hex_digit_display_4 (.value(out_21));
  LED led_4 (.in(flag_out[0]));
  flag_reg flag_reg_1 (.flag_in(flag_in), .flag_in_en(flag_in_en), .clk(clk), .reset(reset), .reg_out(flag_out));
  alu alu_1 (
    .alu_in_1(gp_reg_1_reg_int_out), .alu_in_2({gp_reg_2_reg_int_out_2, gp_reg_2_reg_int_out}),
    .control_word(control_word), .alu_out_en(alu_out_en), .alu_out(out_8), .flag_in(flag_in));
  Hex_Digit_Display #(.decimalPoint("false")) hex_digit_display_5 (.value(gp_reg_1_reg_int_out[7:4]));
  Hex_Digit_Display #(.decimalPoint("false")) hex_digit_display_6 (.value(gp_reg_1_reg_int_out[3:0]));
  Hex_Digit_Display #(.decimalPoint("false")) hex_digit_display_7 (.value(gp_reg_2_reg_int_out_2));
  Hex_Digit_Display #(.decimalPoint("false")) hex_digit_display_8 (.value(gp_reg_2_reg_int_out));
  Hex_Digit_Display #(.decimalPoint("false")) hex_digit_display_9 (.value(control_seq_1_t_state));
  control_seq control_seq_1 (
    .opcode(out_21), .operand(hex), .clk(clk), .boot_loaded(boot_loaded), .cs_reset(reset),
    .flag_state(flag_out), .T_state(control_seq_1_t_state), .a_in_en(a_in_en), .a_out_en(a_out_en),
    .b_in_en(b_in_en), .b_out_en(b_out_en), .alu_out_en(alu_out_en), .control_word(control_word),
    .mar_in_en(mar_in_en), .sram_rd(sram_rd), .sram_wr(sram_wr), .pc_inc(pc_inc), .pc_in_en(pc_in_en),
    .pc_out_en(pc_out_en), .ins_reg_in_en(ins_reg_in_en), .ins_reg_out_en(ins_reg_out_en),
    .flag_in_en(flag_in_en), .hlt(hlt), .pc_reset(in_2));
  Clock u_clk (.out(clk_out));
  not not_1 (reset, power);
  or or_1 (or_1_out, debug, power);
  D_Flip_Flop d_ff_1 (.D(or_2_out), .clk(clk), .Q(power));  // open: Qn, preset, reset
  or or_2 (or_2_out, power, 1'b1);
  not not_2 (not_2_out, hlt);
  D_Flip_Flop #(.trigger("falling")) d_ff_2 (
    .D(or_1_out), .clk(clk), .Q(debug), .reset(boot_loaded));  // open: Qn, preset
  and and_1 (clk, clk_out, not_2_out);
  Hex_Digit_Display hex_digit_display_10 (.value({3'b000, clk_counter_1_ex_bit[0]}));  // open: dp
  clk_counter clk_counter_1 (
    .clk_en(power), .clk(clk), .clk_reset(reset), .extend(power), .count(clk_counter_1_count),
    .ex_bit(clk_counter_1_ex_bit[0]));  // open: count_out_en, count_out, ex_bit_out
  Hex_Digit_Display hex_digit_display_11 (.value(clk_counter_1_count));  // open: dp

  assign out_22 = out_8;

  // Other names for the same wires on the sheet: pc_in[3:0] = hex; pc_reset = in_2; sram_clear = in_1

  // Notes on the sheet:
  //   SRAM
  //   PC
  //   contents of rom_1 (hex, n*v repeats v):
  //   c 1d 63 72 2e f0 6*0 a 5
  //   Accumulator
  //   Reg B
  //   Instruction Reg
  //   S
  //   Z
  //   P
  //   address/shift
  //   opcode
  //   C
  //   ALU
  //   Accumulator
  //   B
  //   CPU Clock
endmodule

module gp_reg (
  input  [7:0] reg_in,
  input  reg_in_en,
  input  reg_clk,
  input  reg_out_en,
  input  reset,
  output [7:0] reg_int_out,
  output [7:0] reg_out
);

  wire multiplexer_1_out, multiplexer_2_out, multiplexer_3_out, multiplexer_4_out, multiplexer_5_out,
       multiplexer_6_out, multiplexer_7_out, multiplexer_8_out;

  Multiplexer multiplexer_1 (.in0(reg_int_out[7]), .in1(reg_in[7]), .out(multiplexer_1_out), .sel(reg_in_en));
  D_Flip_Flop d_ff_1 (.D(multiplexer_1_out), .clk(reg_clk), .Q(reg_int_out[7]), .reset(reset));  // open: Qn, preset
  assign reg_out[7] = reg_out_en ? reg_int_out[7] : 1'bz;  // Controlled_Buffer controlled_buffer_1
  Multiplexer multiplexer_2 (.in0(reg_int_out[6]), .in1(reg_in[6]), .out(multiplexer_2_out), .sel(reg_in_en));
  D_Flip_Flop d_ff_2 (.D(multiplexer_2_out), .clk(reg_clk), .Q(reg_int_out[6]), .reset(reset));  // open: Qn, preset
  assign reg_out[6] = reg_out_en ? reg_int_out[6] : 1'bz;  // Controlled_Buffer controlled_buffer_2
  Multiplexer multiplexer_3 (.in0(reg_int_out[5]), .in1(reg_in[5]), .out(multiplexer_3_out), .sel(reg_in_en));
  D_Flip_Flop d_ff_3 (.D(multiplexer_3_out), .clk(reg_clk), .Q(reg_int_out[5]), .reset(reset));  // open: Qn, preset
  Multiplexer multiplexer_4 (.in0(reg_int_out[4]), .in1(reg_in[4]), .out(multiplexer_4_out), .sel(reg_in_en));
  assign reg_out[5] = reg_out_en ? reg_int_out[5] : 1'bz;  // Controlled_Buffer controlled_buffer_3
  D_Flip_Flop d_ff_4 (.D(multiplexer_4_out), .clk(reg_clk), .Q(reg_int_out[4]), .reset(reset));  // open: Qn, preset
  assign reg_out[4] = reg_out_en ? reg_int_out[4] : 1'bz;  // Controlled_Buffer controlled_buffer_4
  Multiplexer multiplexer_5 (.in0(reg_int_out[3]), .in1(reg_in[3]), .out(multiplexer_5_out), .sel(reg_in_en));
  D_Flip_Flop d_ff_5 (.D(multiplexer_5_out), .clk(reg_clk), .Q(reg_int_out[3]), .reset(reset));  // open: Qn, preset
  Multiplexer multiplexer_6 (.in0(reg_int_out[2]), .in1(reg_in[2]), .out(multiplexer_6_out), .sel(reg_in_en));
  assign reg_out[3] = reg_out_en ? reg_int_out[3] : 1'bz;  // Controlled_Buffer controlled_buffer_5
  D_Flip_Flop d_ff_6 (.D(multiplexer_6_out), .clk(reg_clk), .Q(reg_int_out[2]), .reset(reset));  // open: Qn, preset
  Multiplexer multiplexer_7 (.in0(reg_int_out[1]), .in1(reg_in[1]), .out(multiplexer_7_out), .sel(reg_in_en));
  D_Flip_Flop d_ff_7 (.D(multiplexer_7_out), .clk(reg_clk), .Q(reg_int_out[1]), .reset(reset));  // open: Qn, preset
  assign reg_out[2] = reg_out_en ? reg_int_out[2] : 1'bz;  // Controlled_Buffer controlled_buffer_6
  assign reg_out[1] = reg_out_en ? reg_int_out[1] : 1'bz;  // Controlled_Buffer controlled_buffer_7
  Multiplexer multiplexer_8 (.in0(reg_int_out[0]), .in1(reg_in[0]), .out(multiplexer_8_out), .sel(reg_in_en));
  D_Flip_Flop d_ff_8 (.D(multiplexer_8_out), .clk(reg_clk), .Q(reg_int_out[0]), .reset(reset));  // open: Qn, preset
  assign reg_out[0] = reg_out_en ? reg_int_out[0] : 1'bz;  // Controlled_Buffer controlled_buffer_8

  // Notes on the sheet:
  //   Input Control
  //   Input
  //   Clock
  //   Output Control
  //   Output
  //   Internal Output
endmodule

module alu (
  input  [7:0] alu_in_1,
  input  [7:0] alu_in_2,
  input  [7:0] control_word,
  input  alu_out_en,
  output [7:0] alu_out,
  output [3:0] flag_in
);

  wire carry_adder, carry_flag, carry_shifter;
  wire [1:0] adder_mode, mask_mode, shift_mode;
  wire [7:0] mask_out, reversed_out, shift_out, sum_out;

  adder_sub adder_sub_1 (.A(alu_in_1), .B(alu_in_2), .mode(adder_mode), .sum_out(sum_out), .carry_out(carry_adder));
  shift_rotate shift_rotate_1 (
    .data_in(alu_in_1), .shift_mode(shift_mode), .shift_amount(control_word[2:0]), .data_out(shift_out),
    .carry(carry_shifter));
  bitwise_op bitwise_op_1 (
    .A(alu_in_1), .B(alu_in_2), .op_mode(mask_mode), .biwise_out(mask_out));  // open: or_out, and_out, not_out, xor_out
  reverse_bits reverse_bits_1 (.rev_in(alu_in_1), .rev_out(reversed_out));
  Multiplexer #(.disabled("Z")) multiplexer_1 (
    .in0(carry_adder), .in1(carry_shifter), .out(carry_flag), .sel(control_word[6]));
  Demultiplexer #(.select(2), .width(2)) demultiplexer_1 (
    .out0(adder_mode), .out1(shift_mode), .out2(mask_mode), .in(control_word[5:4]), .sel(control_word[7:6]));  // open: out3
  Multiplexer #(.disabled("Z"), .enable("true"), .select(2), .width(8)) multiplexer_2 (
    .in0(sum_out), .in1(shift_out), .in2(mask_out), .in3(reversed_out), .out(alu_out),
    .sel(control_word[7:6]), .en(alu_out_en));
  flag_updater flag_updater_1 (
    .alu_out(alu_out), .adder_carry_out(carry_flag), .sub_en(adder_mode[0]), .hasCarry(flag_in[0]),
    .isEven(flag_in[1]), .isZero(flag_in[2]), .isNegative(flag_in[3]));

  // Other names for the same wires on the sheet: alu_in1[7:0] = alu_in_1; alu_in2[7:0] = alu_in_2;
  //   shift_amount[2:0] = control_word[2:0]; func_sel[1:0] = control_word[7:6]

  // Notes on the sheet:
  //   A
  //   B
endmodule

module pc (
  input  pc_inc,
  input  pc_in_en,
  input  [3:0] pc_in,
  input  clk,
  input  reset,
  input  pc_out_en,
  output [3:0] pc_value,
  output [3:0] pc_out,
  output c_out
);

  wire and_1_out, and_2_out, and_3_out, and_4_out, and_5_out, and_6_out, and_7_out, and_8_out, and_9_out,
       and_10_out, and_11_out, and_12_out, not_1_out, not_2_out, not_3_out, not_4_out, not_5_out, not_6_out,
       or_1_out, or_2_out, or_3_out, or_4_out, or_5_out, or_6_out, or_7_out, or_8_out;

  not not_1 (not_1_out, pc_in_en);
  not not_2 (not_2_out, pc_in[0]);
  not not_3 (not_3_out, pc_in[1]);
  not not_4 (not_4_out, pc_in[2]);
  not not_5 (not_5_out, pc_in[3]);
  not not_6 (not_6_out, clk);
  and and_1 (and_1_out, pc_inc, not_1_out);
  and and_2 (and_2_out, pc_in_en, pc_in[0]);
  and and_3 (and_3_out, pc_in_en, not_2_out);
  and and_4 (and_4_out, pc_in_en, pc_in[1]);
  and and_5 (and_5_out, pc_in_en, not_3_out);
  and and_6 (and_6_out, pc_in_en, pc_in[2]);
  and and_7 (and_7_out, pc_in_en, not_4_out);
  and and_8 (and_8_out, pc_in_en, pc_in[3]);
  and and_9 (and_9_out, pc_in_en, not_5_out);
  and and_10 (and_10_out, and_1_out, pc_value[0]);
  and and_11 (and_11_out, and_1_out, pc_value[0], pc_value[1]);
  and and_12 (and_12_out, and_1_out, pc_value[0], pc_value[1], pc_value[2]);
  or or_1 (or_1_out, and_2_out, and_1_out);
  or or_2 (or_2_out, and_1_out, and_3_out);
  or or_3 (or_3_out, and_4_out, and_10_out);
  or or_4 (or_4_out, and_10_out, and_5_out);
  or or_5 (or_5_out, and_6_out, and_11_out);
  or or_6 (or_6_out, and_11_out, and_7_out);
  or or_7 (or_7_out, and_8_out, and_12_out);
  or or_8 (or_8_out, and_12_out, and_9_out);
  J_K_Flip_Flop j_k_ff_1 (
    .J(or_1_out), .K(or_2_out), .clk(not_6_out), .Q(pc_value[0]), .reset(reset));  // open: Qn, preset
  J_K_Flip_Flop j_k_ff_2 (
    .J(or_3_out), .K(or_4_out), .clk(not_6_out), .Q(pc_value[1]), .reset(reset));  // open: Qn, preset
  J_K_Flip_Flop j_k_ff_3 (
    .J(or_5_out), .K(or_6_out), .clk(not_6_out), .Q(pc_value[2]), .reset(reset));  // open: Qn, preset
  J_K_Flip_Flop j_k_ff_4 (
    .J(or_7_out), .K(or_8_out), .clk(not_6_out), .Q(pc_value[3]), .reset(reset));  // open: Qn, preset
  and and_13 (c_out, pc_value[3], pc_value[2], pc_value[1], pc_value[0], and_1_out);
  assign pc_out = pc_out_en ? pc_value : 4'bz;  // Controlled_Buffer controlled_buffer_1

  // Other names for the same wires on the sheet: Q0 = pc_value[0]; Q1 = pc_value[1]; Q2 = pc_value[2];
  //   Q3 = pc_value[3]
endmodule

module ins_reg (
  input  [7:0] ins_reg_in,
  input  ins_reg_in_en,
  input  clk,
  input  ins_reg_out_en,
  output [3:0] operand_int,
  output [3:0] operand,
  output [3:0] opcode
);

  gp_reg gp_reg_1 (
    .reg_in(ins_reg_in), .reg_in_en(ins_reg_in_en), .reg_clk(clk), .reg_int_out({opcode, operand_int}));  // open: reg_out_en, reset, reg_out
  assign operand = ins_reg_out_en ? operand_int : 4'bz;  // Controlled_Buffer controlled_buffer_1
endmodule

module sram_cell (
  input  [7:0] data_in,
  input  wr_en,
  input  clk,
  input  cs,
  input  rd_en,
  input  reset,
  output [7:0] memory_content,
  output [7:0] data_out
);

  wire and_1_out, and_2_out;

  and and_1 (and_1_out, wr_en, cs);
  and and_2 (and_2_out, cs, rd_en);
  gp_reg gp_reg_1 (
    .reg_in(data_in), .reg_in_en(and_1_out), .reg_clk(clk), .reg_out_en(and_2_out), .reset(reset),
    .reg_int_out(memory_content), .reg_out(data_out));
endmodule

module dec_4x16 (
  input  [3:0] dec_sel,
  output [15:0] dec_out
);

  wire not_1_out, not_2_out, not_3_out, not_4_out;

  not not_1 (not_1_out, dec_sel[3]);
  not not_2 (not_2_out, dec_sel[2]);
  not not_3 (not_3_out, dec_sel[1]);
  not not_4 (not_4_out, dec_sel[0]);
  and a1 (dec_out[0], not_4_out, not_3_out, not_2_out, not_1_out);
  and a2 (dec_out[1], dec_sel[0], not_3_out, not_2_out, not_1_out);
  and a3 (dec_out[2], not_4_out, dec_sel[1], not_2_out, not_1_out);
  and a4 (dec_out[3], dec_sel[0], dec_sel[1], not_2_out, not_1_out);
  and a5 (dec_out[4], not_4_out, not_3_out, dec_sel[2], not_1_out);
  and a6 (dec_out[5], dec_sel[0], not_3_out, dec_sel[2], not_1_out);
  and a7 (dec_out[6], not_4_out, dec_sel[1], dec_sel[2], not_1_out);
  and a8 (dec_out[7], dec_sel[0], dec_sel[1], dec_sel[2], not_1_out);
  and a9 (dec_out[8], not_4_out, not_3_out, not_2_out, dec_sel[3]);
  and a10 (dec_out[9], dec_sel[0], not_3_out, not_2_out, dec_sel[3]);
  and a11 (dec_out[10], not_4_out, dec_sel[1], not_2_out, dec_sel[3]);
  and a12 (dec_out[11], dec_sel[0], dec_sel[1], not_2_out, dec_sel[3]);
  and a13 (dec_out[12], not_4_out, not_3_out, dec_sel[2], dec_sel[3]);
  and a14 (dec_out[13], dec_sel[0], not_3_out, dec_sel[2], dec_sel[3]);
  and a15 (dec_out[14], not_4_out, dec_sel[1], dec_sel[2], dec_sel[3]);
  and a16 (dec_out[15], dec_sel[0], dec_sel[1], dec_sel[2], dec_sel[3]);
endmodule

module mar (
  input  [7:0] mar_d_in,
  input  mar_in_en,
  input  clk,
  input  reset,
  output cell0,
  output cell1,
  output cell2,
  output cell3,
  output cell4,
  output cell5,
  output cell6,
  output cell7,
  output cell8,
  output cell9,
  output cell10,
  output cell11,
  output cell12,
  output cell13,
  output cell14,
  output cell15
);

  wire [7:0] gp_reg_1_reg_int_out;

  gp_reg gp_reg_1 (
    .reg_in(mar_d_in), .reg_in_en(mar_in_en), .reg_clk(clk), .reset(reset), .reg_int_out(gp_reg_1_reg_int_out));  // open: reg_out_en, reg_out
  dec_4x16 dec_4x16_1 (
    .dec_sel(gp_reg_1_reg_int_out[3:0]),
    .dec_out({cell15, cell14, cell13, cell12, cell11, cell10, cell9, cell8, cell7, cell6, cell5, cell4, cell3, cell2, cell1, cell0}));
endmodule

module sram (
  input  sram_rd,
  input  sram_wr,
  input  [7:0] sram_d_in,
  input  [7:0] mar_d_in,
  input  mar_in_en,
  input  sram_clk,
  input  sram_clear,
  output [7:0] sram_d_out,
  output [7:0] Ox0,
  output [7:0] Ox1,
  output [7:0] Ox2,
  output [7:0] Ox3,
  output [7:0] Ox4,
  output [7:0] Ox5,
  output [7:0] Ox6,
  output [7:0] Ox7,
  output [7:0] Ox8,
  output [7:0] Ox9,
  output [7:0] OxA,
  output [7:0] OxB,
  output [7:0] OxC,
  output [7:0] OxD,
  output [7:0] OxE,
  output [7:0] OxF
);

  wire mar_1_cell0, mar_1_cell1, mar_1_cell2, mar_1_cell3, mar_1_cell4, mar_1_cell5, mar_1_cell6,
       mar_1_cell7, mar_1_cell8, mar_1_cell9, mar_1_cell10, mar_1_cell11, mar_1_cell12, mar_1_cell13,
       mar_1_cell14, mar_1_cell15;
  wire [7:0] controlled_buffer_1_out;

  mar mar_1 (
    .mar_d_in(mar_d_in), .mar_in_en(mar_in_en), .clk(sram_clk), .reset(sram_clear), .cell0(mar_1_cell0),
    .cell1(mar_1_cell1), .cell2(mar_1_cell2), .cell3(mar_1_cell3), .cell4(mar_1_cell4), .cell5(mar_1_cell5),
    .cell6(mar_1_cell6), .cell7(mar_1_cell7), .cell8(mar_1_cell8), .cell9(mar_1_cell9),
    .cell10(mar_1_cell10), .cell11(mar_1_cell11), .cell12(mar_1_cell12), .cell13(mar_1_cell13),
    .cell14(mar_1_cell14), .cell15(mar_1_cell15));
  assign controlled_buffer_1_out = sram_wr ? sram_d_in : 8'bz;  // Controlled_Buffer controlled_buffer_1
  sram_cell sram_cell_1 (
    .data_in(controlled_buffer_1_out), .wr_en(sram_wr), .clk(sram_clk), .cs(mar_1_cell0), .rd_en(sram_rd),
    .reset(sram_clear), .memory_content(Ox0), .data_out(controlled_buffer_1_out));
  sram_cell sram_cell_2 (
    .data_in(controlled_buffer_1_out), .wr_en(sram_wr), .clk(sram_clk), .cs(mar_1_cell1), .rd_en(sram_rd),
    .reset(sram_clear), .memory_content(Ox1), .data_out(controlled_buffer_1_out));
  sram_cell sram_cell_3 (
    .data_in(controlled_buffer_1_out), .wr_en(sram_wr), .clk(sram_clk), .cs(mar_1_cell2), .rd_en(sram_rd),
    .reset(sram_clear), .memory_content(Ox2), .data_out(controlled_buffer_1_out));
  sram_cell sram_cell_4 (
    .data_in(controlled_buffer_1_out), .wr_en(sram_wr), .clk(sram_clk), .cs(mar_1_cell3), .rd_en(sram_rd),
    .reset(sram_clear), .memory_content(Ox3), .data_out(controlled_buffer_1_out));
  sram_cell sram_cell_5 (
    .data_in(controlled_buffer_1_out), .wr_en(sram_wr), .clk(sram_clk), .cs(mar_1_cell4), .rd_en(sram_rd),
    .reset(sram_clear), .memory_content(Ox4), .data_out(controlled_buffer_1_out));
  sram_cell sram_cell_6 (
    .data_in(controlled_buffer_1_out), .wr_en(sram_wr), .clk(sram_clk), .cs(mar_1_cell5), .rd_en(sram_rd),
    .reset(sram_clear), .memory_content(Ox5), .data_out(controlled_buffer_1_out));
  sram_cell sram_cell_7 (
    .data_in(controlled_buffer_1_out), .wr_en(sram_wr), .clk(sram_clk), .cs(mar_1_cell6), .rd_en(sram_rd),
    .reset(sram_clear), .memory_content(Ox6), .data_out(controlled_buffer_1_out));
  sram_cell sram_cell_8 (
    .data_in(controlled_buffer_1_out), .wr_en(sram_wr), .clk(sram_clk), .cs(mar_1_cell7), .rd_en(sram_rd),
    .reset(sram_clear), .memory_content(Ox7), .data_out(controlled_buffer_1_out));
  sram_cell sram_cell_9 (
    .data_in(controlled_buffer_1_out), .wr_en(sram_wr), .clk(sram_clk), .cs(mar_1_cell8), .rd_en(sram_rd),
    .reset(sram_clear), .memory_content(Ox8), .data_out(controlled_buffer_1_out));
  sram_cell sram_cell_10 (
    .data_in(controlled_buffer_1_out), .wr_en(sram_wr), .clk(sram_clk), .cs(mar_1_cell9), .rd_en(sram_rd),
    .reset(sram_clear), .memory_content(Ox9), .data_out(controlled_buffer_1_out));
  sram_cell sram_cell_11 (
    .data_in(controlled_buffer_1_out), .wr_en(sram_wr), .clk(sram_clk), .cs(mar_1_cell10), .rd_en(sram_rd),
    .reset(sram_clear), .memory_content(OxA), .data_out(controlled_buffer_1_out));
  sram_cell sram_cell_12 (
    .data_in(controlled_buffer_1_out), .wr_en(sram_wr), .clk(sram_clk), .cs(mar_1_cell11), .rd_en(sram_rd),
    .reset(sram_clear), .memory_content(OxB), .data_out(controlled_buffer_1_out));
  sram_cell sram_cell_13 (
    .data_in(controlled_buffer_1_out), .wr_en(sram_wr), .clk(sram_clk), .cs(mar_1_cell12), .rd_en(sram_rd),
    .reset(sram_clear), .memory_content(OxC), .data_out(controlled_buffer_1_out));
  sram_cell sram_cell_14 (
    .data_in(controlled_buffer_1_out), .wr_en(sram_wr), .clk(sram_clk), .cs(mar_1_cell13), .rd_en(sram_rd),
    .reset(sram_clear), .memory_content(OxD), .data_out(controlled_buffer_1_out));
  sram_cell sram_cell_15 (
    .data_in(controlled_buffer_1_out), .wr_en(sram_wr), .clk(sram_clk), .cs(mar_1_cell14), .rd_en(sram_rd),
    .reset(sram_clear), .memory_content(OxE), .data_out(controlled_buffer_1_out));
  sram_cell sram_cell_16 (
    .data_in(controlled_buffer_1_out), .wr_en(sram_wr), .clk(sram_clk), .cs(mar_1_cell15), .rd_en(sram_rd),
    .reset(sram_clear), .memory_content(OxF), .data_out(controlled_buffer_1_out));
  assign sram_d_out = sram_rd ? controlled_buffer_1_out : 8'bz;  // Controlled_Buffer controlled_buffer_2
endmodule

module control_seq (
  input  [3:0] opcode,
  input  [3:0] operand,
  input  clk,
  input  boot_loaded,
  input  cs_reset,
  input  [3:0] flag_state,
  output [3:0] T_state,
  output a_in_en,
  output a_out_en,
  output b_in_en,
  output b_out_en,
  output alu_out_en,
  output [7:0] control_word,
  output mar_in_en,
  output sram_rd,
  output sram_wr,
  output pc_inc,
  output pc_in_en,
  output pc_out_en,
  output ins_reg_in_en,
  output ins_reg_out_en,
  output flag_in_en,
  output hlt,
  output pc_reset
);

  wire acc_out, Adder_out, and_1_out, and_2_out, and_3_out, and_4_out, and_5_out, and_6_out, and_7_out,
       and_8_out, and_9_out, and_10_out, and_11_out, and_12_out, and_18_out, and_20_out, BW_out, decode,
       ins_decoder_1_add, ins_decoder_1_bw_and, ins_decoder_1_bw_not, ins_decoder_1_bw_or,
       ins_decoder_1_bw_xor, ins_decoder_1_cmp, ins_decoder_1_dec, ins_decoder_1_hlt, ins_decoder_1_inc,
       ins_decoder_1_jmp, ins_decoder_1_jnz, ins_decoder_1_jz, ins_decoder_1_lda, ins_decoder_1_ldb,
       ins_decoder_1_nop, ins_decoder_1_rev, ins_decoder_1_rl, ins_decoder_1_rr, ins_decoder_1_shl,
       ins_decoder_1_shr, ins_decoder_1_sta, ins_decoder_1_sub, Jump_out, mov_out, not_1_out, or_2_out,
       or_3_out, or_4_out, or_5_out, or_6_out, or_7_out, or_8_out, or_9_out, or_10_out, Shift_out, T1, T2,
       T3, T4, T5;

  ins_decoder ins_decoder_1 (
    .opcode(opcode), .decode(decode), .operand(operand), .LDA(ins_decoder_1_lda), .LDB(ins_decoder_1_ldb),
    .STA(ins_decoder_1_sta), .JMP(ins_decoder_1_jmp), .JZ(ins_decoder_1_jz), .JNZ(ins_decoder_1_jnz),
    .SHL(ins_decoder_1_shl), .SHR(ins_decoder_1_shr), .RL(ins_decoder_1_rl), .RR(ins_decoder_1_rr),
    .ADD(ins_decoder_1_add), .SUB(ins_decoder_1_sub), .INC(ins_decoder_1_inc), .DEC(ins_decoder_1_dec),
    .REV(ins_decoder_1_rev), .HLT(ins_decoder_1_hlt), .NOP(ins_decoder_1_nop), .CMP(ins_decoder_1_cmp),
    .BW_OR(ins_decoder_1_bw_or), .BW_AND(ins_decoder_1_bw_and), .BW_NOT(ins_decoder_1_bw_not),
    .BW_XOR(ins_decoder_1_bw_xor));
  or BW (BW_out, ins_decoder_1_bw_or, ins_decoder_1_bw_and, ins_decoder_1_bw_not, ins_decoder_1_bw_xor);
  or mov (mov_out, ins_decoder_1_lda, ins_decoder_1_ldb, ins_decoder_1_sta);
  or Jump (Jump_out, ins_decoder_1_jmp, ins_decoder_1_jz, ins_decoder_1_jnz);
  or Shift (Shift_out, ins_decoder_1_shl, ins_decoder_1_shr, ins_decoder_1_rl, ins_decoder_1_rr);
  or Adder (Adder_out, ins_decoder_1_add, ins_decoder_1_sub, ins_decoder_1_inc, ins_decoder_1_dec);
  or acc (acc_out, BW_out, Shift_out, Adder_out, ins_decoder_1_rev);
  or or_1 (decode, T4, T5);
  or or_2 (or_2_out, ins_decoder_1_sub, ins_decoder_1_cmp);
  or or_3 (or_3_out, acc_out, ins_decoder_1_lda);
  or or_4 (or_4_out, acc_out, ins_decoder_1_cmp);
  and and_1 (and_1_out, mov_out, T4);
  or or_5 (or_5_out, ins_decoder_1_lda, ins_decoder_1_ldb);
  and and_2 (and_2_out, ins_decoder_1_sta, T5);
  or or_6 (or_6_out, Jump_out, mov_out);
  not not_1 (not_1_out, flag_state[2]);
  and and_3 (and_3_out, not_1_out, ins_decoder_1_jnz);
  and and_4 (and_4_out, flag_state[2], ins_decoder_1_jz);
  or or_7 (or_7_out, acc_out, ins_decoder_1_cmp);
  and and_5 (and_5_out, or_3_out, T5);
  and and_6 (and_6_out, ins_decoder_1_sta, T5);
  and and_7 (and_7_out, ins_decoder_1_ldb, T5);
  and and_8 (and_8_out, or_4_out, T5);
  or or_8 (or_8_out, and_1_out, T1);
  and and_9 (and_9_out, or_5_out, T5);
  and and_10 (and_10_out, or_6_out, T4);
  or or_9 (or_9_out, and_9_out, T2);
  or or_10 (or_10_out, and_3_out, and_4_out, ins_decoder_1_jmp);
  and and_11 (and_11_out, or_10_out, T4);
  and and_12 (and_12_out, ins_decoder_1_hlt, T4);
  alu_controls alu_controls_1 (
    .SHL(ins_decoder_1_shl), .SHR(ins_decoder_1_shr), .RL(ins_decoder_1_rl), .RR(ins_decoder_1_rr),
    .ADD(ins_decoder_1_add), .SUB(or_2_out), .INC(ins_decoder_1_inc), .DEC(ins_decoder_1_dec),
    .BW_OR(ins_decoder_1_bw_or), .BW_AND(ins_decoder_1_bw_and), .BW_NOT(ins_decoder_1_bw_not),
    .BW_XOR(ins_decoder_1_bw_xor), .Reverse(ins_decoder_1_rev), .operand(operand), .control_word(control_word));
  and and_13 (a_in_en, boot_loaded, and_5_out);
  and and_14 (a_out_en, boot_loaded, and_6_out);
  and and_15 (b_in_en, boot_loaded, and_7_out);
  and and_16 (b_out_en, boot_loaded, 1'b0);
  and and_17 (alu_out_en, boot_loaded, and_8_out);
  and and_18 (and_18_out, boot_loaded, or_8_out);
  assign mar_in_en = boot_loaded ? and_18_out : 1'bz;  // Controlled_Buffer controlled_buffer_1
  and and_19 (sram_rd, boot_loaded, or_9_out);
  and and_20 (and_20_out, boot_loaded, and_2_out);
  assign sram_wr = boot_loaded ? and_20_out : 1'bz;  // Controlled_Buffer controlled_buffer_2
  and and_21 (ins_reg_in_en, boot_loaded, T2);
  and and_22 (ins_reg_out_en, boot_loaded, and_10_out);
  and and_23 (pc_inc, boot_loaded, T3);
  and and_24 (pc_in_en, boot_loaded, and_11_out);
  and and_25 (pc_out_en, boot_loaded, T1);
  and and_26 (flag_in_en, boot_loaded, T5, or_7_out);
  and and_27 (hlt, boot_loaded, and_12_out);
  ring_counter_5x ring_counter_5x_1 (
    .pc_inc(boot_loaded), .clk(clk), .reset(cs_reset), .T_state(T_state), .T1(T1), .T2(T2), .T3(T3), .T4(T4),
    .T5(T5));

  // Other names for the same wires on the sheet: loaded = boot_loaded; reset = cs_reset
endmodule

module ins_decoder (
  input  [3:0] opcode,
  input  decode,
  input  [3:0] operand,
  output LDA,
  output LDB,
  output STA,
  output JMP,
  output JZ,
  output JNZ,
  output SHL,
  output SHR,
  output RL,
  output RR,
  output ADD,
  output SUB,
  output INC,
  output DEC,
  output REV,
  output HLT,
  output NOP,
  output CMP,
  output BW_OR,
  output BW_AND,
  output BW_NOT,
  output BW_XOR
);

  wire not_1_out;
  wire [15:0] dec_4x16_1_dec_out;

  not not_1 (not_1_out, operand[0]);
  dec_4x16 dec_4x16_1 (.dec_sel(opcode), .dec_out(dec_4x16_1_dec_out));
  and and_1 (LDA, dec_4x16_1_dec_out[0], decode);
  and and_2 (LDB, dec_4x16_1_dec_out[1], decode);
  and and_3 (STA, dec_4x16_1_dec_out[2], decode);
  and and_4 (JMP, dec_4x16_1_dec_out[3], decode);
  and and_5 (JZ, dec_4x16_1_dec_out[4], decode);
  and and_6 (JNZ, dec_4x16_1_dec_out[5], decode);
  and and_7 (SHL, dec_4x16_1_dec_out[6], decode);
  and and_8 (SHR, dec_4x16_1_dec_out[7], decode);
  and and_9 (RL, dec_4x16_1_dec_out[8], decode);
  and and_10 (RR, dec_4x16_1_dec_out[9], decode);
  and and_11 (ADD, dec_4x16_1_dec_out[10], not_1_out, decode);
  and and_12 (SUB, dec_4x16_1_dec_out[11], not_1_out, decode);
  and and_13 (INC, dec_4x16_1_dec_out[12], not_1_out, decode);
  and and_14 (DEC, dec_4x16_1_dec_out[13], not_1_out, decode);
  and and_15 (REV, dec_4x16_1_dec_out[14], not_1_out, decode);
  and and_16 (HLT, dec_4x16_1_dec_out[15], not_1_out, decode);
  and and_17 (NOP, dec_4x16_1_dec_out[10], operand[0], decode);
  and and_18 (CMP, dec_4x16_1_dec_out[11], operand[0], decode);
  and and_19 (BW_OR, dec_4x16_1_dec_out[12], operand[0], decode);
  and and_20 (BW_AND, dec_4x16_1_dec_out[13], operand[0], decode);
  and and_21 (BW_NOT, dec_4x16_1_dec_out[14], operand[0], decode);
  and and_22 (BW_XOR, dec_4x16_1_dec_out[15], operand[0], decode);
endmodule

module alu_controls (
  input  SHL,
  input  SHR,
  input  RL,
  input  RR,
  input  ADD,
  input  SUB,
  input  INC,
  input  DEC,
  input  BW_OR,
  input  BW_AND,
  input  BW_NOT,
  input  BW_XOR,
  input  Reverse,
  input  [3:0] operand,
  output [7:0] control_word
);

  wire not_1_out, not_2_out, not_3_out, or_1_out, or_2_out, or_3_out, or_4_out, or_5_out, or_6_out, or_7_out,
       or_8_out, or_9_out;

  or or_1 (or_1_out, ADD, SUB, INC, DEC);
  not not_1 (not_1_out, or_1_out);
  or or_2 (or_2_out, SHL, SHR, RL, RR);
  not not_2 (not_2_out, or_2_out);
  or or_3 (or_3_out, BW_OR, BW_AND, BW_NOT, BW_XOR);
  not not_3 (not_3_out, or_3_out);
  or or_4 (or_4_out, DEC, INC);
  or or_5 (or_5_out, RR, RL);
  or or_6 (or_6_out, BW_XOR, BW_NOT);
  or or_7 (or_7_out, SUB, DEC);
  or or_8 (or_8_out, SHR, RR);
  or or_9 (or_9_out, BW_AND, BW_XOR);
  or or_10 (control_word[5], Reverse, or_4_out, or_5_out, or_6_out);
  or or_11 (control_word[4], Reverse, or_7_out, or_8_out, or_9_out);
  or or_12 (control_word[7], or_3_out, Reverse);
  or or_13 (control_word[6], or_2_out, Reverse);

  assign control_word[3:0] = operand;
endmodule

module bootloader (
  input  reset,
  input  en,
  input  clk,
  input  [7:0] sram_data,
  output [7:0] debug_data,
  output mar_in_en,
  output sram_wr,
  output boot_loaded,
  output [7:0] sram_addr
);

  wire and_1_out, and_2_out, and_3_out, and_4_out, clk_t, d_ff_1_q, mar_in_en_t, nand_1_out, not_2_out,
       not_3_out, or_1_out, or_2_out, sram_wr_t, started;
  wire [7:0] multiplexer_1_out;

  and and_1 (and_1_out, started, clk_t);
  or or_1 (or_1_out, started, en);
  D_Flip_Flop #(.trigger("falling")) d_ff_1 (
    .D(mar_in_en_t), .clk(and_1_out), .Q(d_ff_1_q), .Qn(mar_in_en_t), .reset(reset));  // open: preset
  D_Flip_Flop #(.trigger("falling")) d_ff_2 (
    .D(or_1_out), .clk(clk_t), .Q(started), .reset(reset));  // open: Qn, preset
  not not_1 (sram_wr_t, mar_in_en_t);
  pc pc_1 (
    .pc_inc(en), .clk(d_ff_1_q), .reset(reset), .pc_value(sram_addr[3:0]));  // open: pc_in_en, pc_in, pc_out_en, pc_out, c_out
  Hex_Digit_Display #(.decimalPoint("false")) hex_digit_display_1 (.value(sram_addr[3:0]));
  nand nand_1 (nand_1_out, sram_addr[0], sram_addr[1], sram_addr[2], sram_addr[3]);
  D_Flip_Flop d_ff_3 (.D(or_2_out), .clk(nand_1_out), .Q(boot_loaded), .reset(reset));  // open: Qn, preset
  or or_2 (or_2_out, boot_loaded, 1'b1);
  not not_2 (not_2_out, boot_loaded);
  not not_3 (not_3_out, boot_loaded);
  and and_2 (and_2_out, en, not_2_out);
  Multiplexer #(.width(8)) multiplexer_1 (
    .in0({4'b0000, sram_addr[3:0]}), .in1(sram_data), .out(multiplexer_1_out), .sel(sram_wr_t));
  and and_3 (and_3_out, sram_wr_t, started);
  assign debug_data = started ? multiplexer_1_out : 8'bz;  // Controlled_Buffer controlled_buffer_1
  and and_4 (and_4_out, mar_in_en_t, started);
  assign sram_wr = and_2_out ? and_3_out : 1'bz;  // Controlled_Buffer controlled_buffer_2
  and and_5 (clk_t, clk, not_3_out, en);
  assign mar_in_en = and_2_out ? and_4_out : 1'bz;  // Controlled_Buffer controlled_buffer_3

  assign sram_addr[7:4] = 4'b0000;
endmodule

module flag_reg (
  input  [3:0] flag_in,
  input  flag_in_en,
  input  clk,
  input  reset,
  output [3:0] reg_out
);

  wire and_1_out;

  and and_1 (and_1_out, flag_in_en, clk);
  D_Flip_Flop d_ff_1 (.D(flag_in[3]), .clk(and_1_out), .Q(reg_out[3]), .reset(reset));  // open: Qn, preset
  D_Flip_Flop d_ff_2 (.D(flag_in[2]), .clk(and_1_out), .Q(reg_out[2]), .reset(reset));  // open: Qn, preset
  D_Flip_Flop d_ff_3 (.D(flag_in[1]), .clk(and_1_out), .Q(reg_out[1]), .reset(reset));  // open: Qn, preset
  D_Flip_Flop d_ff_4 (.D(flag_in[0]), .clk(and_1_out), .Q(reg_out[0]), .reset(reset));  // open: Qn, preset

  // Notes on the sheet:
  //   parity flag
  //   sign
  //   zero
  //   carry
endmodule

module clk_counter (
  input  clk_en,
  input  clk,
  input  clk_reset,
  input  extend,
  input  count_out_en,
  output [3:0] count,
  output [3:0] count_out,
  output ex_bit,
  output ex_bit_out
);

  wire j_k_ff_1_q, j_k_ff_2_qn, j_k_ff_3_qn, j_k_ff_4_qn, j_k_ff_5_qn, not_1_out;

  J_K_Flip_Flop j_k_ff_1 (
    .J(clk_en), .K(clk_en), .clk(j_k_ff_2_qn), .Q(j_k_ff_1_q), .reset(clk_reset));  // open: Qn, preset
  not not_1 (not_1_out, clk);
  J_K_Flip_Flop j_k_ff_2 (
    .J(clk_en), .K(clk_en), .clk(j_k_ff_3_qn), .Q(count[3]), .Qn(j_k_ff_2_qn), .reset(clk_reset));  // open: preset
  J_K_Flip_Flop j_k_ff_3 (
    .J(clk_en), .K(clk_en), .clk(j_k_ff_4_qn), .Q(count[2]), .Qn(j_k_ff_3_qn), .reset(clk_reset));  // open: preset
  J_K_Flip_Flop j_k_ff_4 (
    .J(clk_en), .K(clk_en), .clk(j_k_ff_5_qn), .Q(count[1]), .Qn(j_k_ff_4_qn), .reset(clk_reset));  // open: preset
  J_K_Flip_Flop j_k_ff_5 (
    .J(clk_en), .K(clk_en), .clk(not_1_out), .Q(count[0]), .Qn(j_k_ff_5_qn), .reset(clk_reset));  // open: preset
  assign ex_bit = extend ? j_k_ff_1_q : 1'bz;  // Controlled_Buffer controlled_buffer_1
  assign count_out = count_out_en ? count : 4'bz;  // Controlled_Buffer controlled_buffer_2
  assign ex_bit_out = count_out_en ? ex_bit : 1'bz;  // Controlled_Buffer controlled_buffer_3

  // Notes on the sheet:
  //   Output Control
  //   Clock
  //   Reset
  //   Counter Control
endmodule

module ring_counter_5x (
  input  pc_inc,
  input  clk,
  input  reset,
  output [3:0] T_state,
  output T1,
  output T2,
  output T3,
  output T4,
  output T5
);

  wire [15:0] dec_4x16_1_dec_out;

  pc pc_1 (
    .pc_inc(pc_inc), .pc_in_en(T5), .pc_in({3'b000, pc_inc}), .clk(clk), .reset(reset), .pc_value(T_state));  // open: pc_out_en, pc_out, c_out
  dec_4x16 dec_4x16_1 (
    .dec_sel(T_state), .dec_out({dec_4x16_1_dec_out[15:6], T5, T4, T3, T2, T1, dec_4x16_1_dec_out[0]}));
endmodule

module adder_sub (
  input  [7:0] A,
  input  [7:0] B,
  input  [1:0] mode,
  output [7:0] sum_out,
  output carry_out
);

  wire adder_2_cout, adder_3_cout, adder_4_cout, adder_5_cout, adder_6_cout, adder_7_cout, adder_8_cout,
       decoder_1_out1, decoder_1_out2, decoder_1_out3, or_1_out, sub_en, xor_1_out, xor_2_out, xor_3_out,
       xor_4_out, xor_5_out, xor_6_out, xor_7_out, xor_8_out;
  wire [7:0] multiplexer_1_out;

  xor xor_1 (xor_1_out, multiplexer_1_out[7], sub_en);
  Adder #(.width(1)) adder_1 (.a(A[7]), .b(xor_1_out), .out(sum_out[7]), .cin(adder_2_cout), .cout(carry_out));
  Adder #(.width(1)) adder_2 (.a(A[6]), .b(xor_2_out), .out(sum_out[6]), .cin(adder_3_cout), .cout(adder_2_cout));
  xor xor_2 (xor_2_out, multiplexer_1_out[6], sub_en);
  Adder #(.width(1)) adder_3 (.a(A[5]), .b(xor_3_out), .out(sum_out[5]), .cin(adder_4_cout), .cout(adder_3_cout));
  xor xor_3 (xor_3_out, multiplexer_1_out[5], sub_en);
  xor xor_4 (xor_4_out, multiplexer_1_out[4], sub_en);
  Adder #(.width(1)) adder_4 (.a(A[4]), .b(xor_4_out), .out(sum_out[4]), .cin(adder_5_cout), .cout(adder_4_cout));
  xor xor_5 (xor_5_out, multiplexer_1_out[3], sub_en);
  Adder #(.width(1)) adder_5 (.a(A[3]), .b(xor_5_out), .out(sum_out[3]), .cin(adder_6_cout), .cout(adder_5_cout));
  xor xor_6 (xor_6_out, multiplexer_1_out[2], sub_en);
  Adder #(.width(1)) adder_6 (.a(A[2]), .b(xor_6_out), .out(sum_out[2]), .cin(adder_7_cout), .cout(adder_6_cout));
  Decoder #(.enable("false"), .select(2)) decoder_1 (
    .out1(decoder_1_out1), .out2(decoder_1_out2), .out3(decoder_1_out3), .sel(mode));  // open: out0
  Adder #(.width(1)) adder_7 (.a(A[1]), .b(xor_7_out), .out(sum_out[1]), .cin(adder_8_cout), .cout(adder_7_cout));
  xor xor_7 (xor_7_out, multiplexer_1_out[1], sub_en);
  xor xor_8 (xor_8_out, multiplexer_1_out[0], sub_en);
  Multiplexer #(.width(8)) multiplexer_1 (.in0(B), .in1(8'h1), .out(multiplexer_1_out), .sel(or_1_out));
  or or_1 (or_1_out, decoder_1_out2, decoder_1_out3);
  or or_2 (sub_en, decoder_1_out1, decoder_1_out3);
  Adder #(.width(1)) adder_8 (.a(A[0]), .b(xor_8_out), .out(sum_out[0]), .cin(sub_en), .cout(adder_8_cout));

  // Notes on the sheet:
  //   Input1
  //   Carry/Borrow'
  //   Subtract Control
  //   Input2
  //   Output
endmodule

module bitwise_AND (
  input  [7:0] A,
  input  [7:0] B,
  output Q7,
  output Q6,
  output Q5,
  output Q4,
  output Q3,
  output Q2,
  output Q1,
  output Q0
);

  and and_1 (Q7, A[7], B[7]);
  and and_2 (Q6, A[6], B[6]);
  and and_3 (Q5, A[5], B[5]);
  and and_4 (Q4, A[4], B[4]);
  and and_5 (Q3, A[3], B[3]);
  and and_6 (Q2, A[2], B[2]);
  and and_7 (Q1, A[1], B[1]);
  and and_8 (Q0, A[0], B[0]);
endmodule

module bitwise_OR (
  input  [7:0] A,
  input  [7:0] B,
  output Q7,
  output Q6,
  output Q5,
  output Q4,
  output Q3,
  output Q2,
  output Q1,
  output Q0
);

  or or_1 (Q7, A[7], B[7]);
  or or_2 (Q6, A[6], B[6]);
  or or_3 (Q5, A[5], B[5]);
  or or_4 (Q4, A[4], B[4]);
  or or_5 (Q3, A[3], B[3]);
  or or_6 (Q2, A[2], B[2]);
  or or_7 (Q1, A[1], B[1]);
  or or_8 (Q0, A[0], B[0]);
endmodule

module bitwise_NOT (
  input  [7:0] A,
  output Q7,
  output Q6,
  output Q5,
  output Q4,
  output Q3,
  output Q2,
  output Q1,
  output Q0
);

  not not_1 (Q7, A[7]);
  not not_2 (Q6, A[6]);
  not not_3 (Q5, A[5]);
  not not_4 (Q4, A[4]);
  not not_5 (Q3, A[3]);
  not not_6 (Q2, A[2]);
  not not_7 (Q1, A[1]);
  not not_8 (Q0, A[0]);
endmodule

module bitwise_XOR (
  input  [7:0] A,
  input  [7:0] B,
  output Q7,
  output Q6,
  output Q5,
  output Q4,
  output Q3,
  output Q2,
  output Q1,
  output Q0
);

  xor xor_1 (Q7, A[7], B[7]);
  xor xor_2 (Q6, A[6], B[6]);
  xor xor_3 (Q5, A[5], B[5]);
  xor xor_4 (Q4, A[4], B[4]);
  xor xor_5 (Q3, A[3], B[3]);
  xor xor_6 (Q2, A[2], B[2]);
  xor xor_7 (Q1, A[1], B[1]);
  xor xor_8 (Q0, A[0], B[0]);
endmodule

module bitwise_op (
  input  [7:0] A,
  input  [7:0] B,
  input  [1:0] op_mode,
  output [7:0] biwise_out,
  output [7:0] or_out,
  output [7:0] and_out,
  output [7:0] not_out,
  output [7:0] xor_out
);

  bitwise_OR bitwise_or_1 (
    .A(A), .B(B), .Q7(or_out[7]), .Q6(or_out[6]), .Q5(or_out[5]), .Q4(or_out[4]), .Q3(or_out[3]),
    .Q2(or_out[2]), .Q1(or_out[1]), .Q0(or_out[0]));
  bitwise_AND bitwise_and_1 (
    .A(A), .B(B), .Q7(and_out[7]), .Q6(and_out[6]), .Q5(and_out[5]), .Q4(and_out[4]), .Q3(and_out[3]),
    .Q2(and_out[2]), .Q1(and_out[1]), .Q0(and_out[0]));
  bitwise_NOT bitwise_not_1 (
    .A(A), .Q7(not_out[7]), .Q6(not_out[6]), .Q5(not_out[5]), .Q4(not_out[4]), .Q3(not_out[3]),
    .Q2(not_out[2]), .Q1(not_out[1]), .Q0(not_out[0]));
  bitwise_XOR bitwise_xor_1 (
    .A(A), .B(B), .Q7(xor_out[7]), .Q6(xor_out[6]), .Q5(xor_out[5]), .Q4(xor_out[4]), .Q3(xor_out[3]),
    .Q2(xor_out[2]), .Q1(xor_out[1]), .Q0(xor_out[0]));
  Multiplexer #(.select(2), .width(8)) multiplexer_1 (
    .in0(or_out), .in1(and_out), .in2(not_out), .in3(xor_out), .out(biwise_out), .sel(op_mode));
endmodule

module reverse_bits (
  input  [7:0] rev_in,
  output [7:0] rev_out
);


  assign rev_out = {rev_in[0], rev_in[1], rev_in[2], rev_in[3], rev_in[4], rev_in[5], rev_in[6], rev_in[7]};
endmodule

module left_shifter (
  input  [7:0] shift_in,
  input  [2:0] shift_amount,
  output [7:0] shifted_out
);

  wire multiplexer_1_out, multiplexer_2_out, multiplexer_3_out, multiplexer_4_out, multiplexer_5_out,
       multiplexer_6_out, multiplexer_7_out, multiplexer_8_out, multiplexer_9_out, multiplexer_10_out,
       multiplexer_11_out, multiplexer_12_out, multiplexer_13_out, multiplexer_14_out, multiplexer_15_out,
       multiplexer_16_out;

  Multiplexer multiplexer_1 (.in0(shift_in[7]), .in1(shift_in[6]), .out(multiplexer_1_out), .sel(shift_amount[0]));
  Multiplexer multiplexer_2 (.in0(shift_in[6]), .in1(shift_in[5]), .out(multiplexer_2_out), .sel(shift_amount[0]));
  Multiplexer multiplexer_3 (.in0(shift_in[5]), .in1(shift_in[4]), .out(multiplexer_3_out), .sel(shift_amount[0]));
  Multiplexer multiplexer_4 (.in0(shift_in[4]), .in1(shift_in[3]), .out(multiplexer_4_out), .sel(shift_amount[0]));
  Multiplexer multiplexer_5 (.in0(shift_in[3]), .in1(shift_in[2]), .out(multiplexer_5_out), .sel(shift_amount[0]));
  Multiplexer multiplexer_6 (.in0(shift_in[2]), .in1(shift_in[1]), .out(multiplexer_6_out), .sel(shift_amount[0]));
  Multiplexer multiplexer_7 (.in0(shift_in[1]), .in1(shift_in[0]), .out(multiplexer_7_out), .sel(shift_amount[0]));
  Multiplexer multiplexer_8 (.in0(shift_in[0]), .in1(1'b0), .out(multiplexer_8_out), .sel(shift_amount[0]));
  Multiplexer multiplexer_9 (
    .in0(multiplexer_1_out), .in1(multiplexer_3_out), .out(multiplexer_9_out), .sel(shift_amount[1]));
  Multiplexer multiplexer_10 (
    .in0(multiplexer_2_out), .in1(multiplexer_4_out), .out(multiplexer_10_out), .sel(shift_amount[1]));
  Multiplexer multiplexer_11 (
    .in0(multiplexer_3_out), .in1(multiplexer_5_out), .out(multiplexer_11_out), .sel(shift_amount[1]));
  Multiplexer multiplexer_12 (
    .in0(multiplexer_4_out), .in1(multiplexer_6_out), .out(multiplexer_12_out), .sel(shift_amount[1]));
  Multiplexer multiplexer_13 (
    .in0(multiplexer_5_out), .in1(multiplexer_7_out), .out(multiplexer_13_out), .sel(shift_amount[1]));
  Multiplexer multiplexer_14 (
    .in0(multiplexer_6_out), .in1(multiplexer_8_out), .out(multiplexer_14_out), .sel(shift_amount[1]));
  Multiplexer multiplexer_15 (.in0(multiplexer_7_out), .in1(1'b0), .out(multiplexer_15_out), .sel(shift_amount[1]));
  Multiplexer multiplexer_16 (.in0(multiplexer_8_out), .in1(1'b0), .out(multiplexer_16_out), .sel(shift_amount[1]));
  Multiplexer multiplexer_17 (
    .in0(multiplexer_9_out), .in1(multiplexer_13_out), .out(shifted_out[7]), .sel(shift_amount[2]));
  Multiplexer multiplexer_18 (
    .in0(multiplexer_10_out), .in1(multiplexer_14_out), .out(shifted_out[6]), .sel(shift_amount[2]));
  Multiplexer multiplexer_19 (
    .in0(multiplexer_11_out), .in1(multiplexer_15_out), .out(shifted_out[5]), .sel(shift_amount[2]));
  Multiplexer multiplexer_20 (.in0(multiplexer_12_out), .in1(1'b0), .out(shifted_out[4]), .sel(shift_amount[2]));
  Multiplexer multiplexer_21 (.in0(multiplexer_13_out), .in1(1'b0), .out(shifted_out[3]), .sel(shift_amount[2]));
  Multiplexer multiplexer_22 (.in0(multiplexer_14_out), .in1(1'b0), .out(shifted_out[2]), .sel(shift_amount[2]));
  Multiplexer multiplexer_23 (.in0(multiplexer_15_out), .in1(1'b0), .out(shifted_out[1]), .sel(shift_amount[2]));
  Multiplexer multiplexer_24 (.in0(multiplexer_16_out), .in1(1'b0), .out(shifted_out[0]), .sel(shift_amount[2]));
endmodule

module barrel_shifter (
  input  [7:0] shift_in,
  input  direction,
  input  [2:0] shift_amount,
  output [7:0] shift_out
);

  wire [7:0] left_shifter_1_shifted_out, multiplexer_1_out, reverse_bits_1_rev_out, reverse_bits_2_rev_out;

  reverse_bits reverse_bits_1 (.rev_in(shift_in), .rev_out(reverse_bits_1_rev_out));
  Multiplexer #(.width(8)) multiplexer_1 (
    .in0(shift_in), .in1(reverse_bits_1_rev_out), .out(multiplexer_1_out), .sel(direction));
  left_shifter left_shifter_1 (
    .shift_in(multiplexer_1_out), .shift_amount(shift_amount), .shifted_out(left_shifter_1_shifted_out));
  reverse_bits reverse_bits_2 (.rev_in(left_shifter_1_shifted_out), .rev_out(reverse_bits_2_rev_out));
  Multiplexer #(.width(8)) multiplexer_2 (
    .in0(left_shifter_1_shifted_out), .in1(reverse_bits_2_rev_out), .out(shift_out), .sel(direction));
endmodule

module left_rotator (
  input  [7:0] rotate_in,
  input  [2:0] shift_amount,
  output [7:0] rotate_out
);

  wire multiplexer_1_out, multiplexer_2_out, multiplexer_3_out, multiplexer_4_out, multiplexer_5_out,
       multiplexer_6_out, multiplexer_7_out, multiplexer_8_out, multiplexer_9_out, multiplexer_10_out,
       multiplexer_11_out, multiplexer_12_out, multiplexer_13_out, multiplexer_14_out, multiplexer_15_out,
       multiplexer_16_out;

  Multiplexer multiplexer_1 (.in0(rotate_in[7]), .in1(rotate_in[6]), .out(multiplexer_1_out), .sel(shift_amount[0]));
  Multiplexer multiplexer_2 (.in0(rotate_in[6]), .in1(rotate_in[5]), .out(multiplexer_2_out), .sel(shift_amount[0]));
  Multiplexer multiplexer_3 (.in0(rotate_in[5]), .in1(rotate_in[4]), .out(multiplexer_3_out), .sel(shift_amount[0]));
  Multiplexer multiplexer_4 (.in0(rotate_in[4]), .in1(rotate_in[3]), .out(multiplexer_4_out), .sel(shift_amount[0]));
  Multiplexer multiplexer_5 (.in0(rotate_in[3]), .in1(rotate_in[2]), .out(multiplexer_5_out), .sel(shift_amount[0]));
  Multiplexer multiplexer_6 (.in0(rotate_in[2]), .in1(rotate_in[1]), .out(multiplexer_6_out), .sel(shift_amount[0]));
  Multiplexer multiplexer_7 (.in0(rotate_in[1]), .in1(rotate_in[0]), .out(multiplexer_7_out), .sel(shift_amount[0]));
  Multiplexer multiplexer_8 (.in0(rotate_in[0]), .in1(rotate_in[7]), .out(multiplexer_8_out), .sel(shift_amount[0]));
  Multiplexer multiplexer_9 (
    .in0(multiplexer_1_out), .in1(multiplexer_3_out), .out(multiplexer_9_out), .sel(shift_amount[1]));
  Multiplexer multiplexer_10 (
    .in0(multiplexer_2_out), .in1(multiplexer_4_out), .out(multiplexer_10_out), .sel(shift_amount[1]));
  Multiplexer multiplexer_11 (
    .in0(multiplexer_3_out), .in1(multiplexer_5_out), .out(multiplexer_11_out), .sel(shift_amount[1]));
  Multiplexer multiplexer_12 (
    .in0(multiplexer_4_out), .in1(multiplexer_6_out), .out(multiplexer_12_out), .sel(shift_amount[1]));
  Multiplexer multiplexer_13 (
    .in0(multiplexer_5_out), .in1(multiplexer_7_out), .out(multiplexer_13_out), .sel(shift_amount[1]));
  Multiplexer multiplexer_14 (
    .in0(multiplexer_6_out), .in1(multiplexer_8_out), .out(multiplexer_14_out), .sel(shift_amount[1]));
  Multiplexer multiplexer_15 (
    .in0(multiplexer_7_out), .in1(multiplexer_1_out), .out(multiplexer_15_out), .sel(shift_amount[1]));
  Multiplexer multiplexer_16 (
    .in0(multiplexer_8_out), .in1(multiplexer_2_out), .out(multiplexer_16_out), .sel(shift_amount[1]));
  Multiplexer multiplexer_17 (
    .in0(multiplexer_9_out), .in1(multiplexer_13_out), .out(rotate_out[7]), .sel(shift_amount[2]));
  Multiplexer multiplexer_18 (
    .in0(multiplexer_10_out), .in1(multiplexer_14_out), .out(rotate_out[6]), .sel(shift_amount[2]));
  Multiplexer multiplexer_19 (
    .in0(multiplexer_11_out), .in1(multiplexer_15_out), .out(rotate_out[5]), .sel(shift_amount[2]));
  Multiplexer multiplexer_20 (
    .in0(multiplexer_12_out), .in1(multiplexer_16_out), .out(rotate_out[4]), .sel(shift_amount[2]));
  Multiplexer multiplexer_21 (
    .in0(multiplexer_13_out), .in1(multiplexer_9_out), .out(rotate_out[3]), .sel(shift_amount[2]));
  Multiplexer multiplexer_22 (
    .in0(multiplexer_14_out), .in1(multiplexer_10_out), .out(rotate_out[2]), .sel(shift_amount[2]));
  Multiplexer multiplexer_23 (
    .in0(multiplexer_15_out), .in1(multiplexer_11_out), .out(rotate_out[1]), .sel(shift_amount[2]));
  Multiplexer multiplexer_24 (
    .in0(multiplexer_16_out), .in1(multiplexer_12_out), .out(rotate_out[0]), .sel(shift_amount[2]));
endmodule

module barrel_rotator (
  input  [7:0] rotate_in,
  input  direction,
  input  [2:0] shift_amount,
  output [7:0] rotate_out
);

  wire [7:0] left_rotator_1_rotate_out, multiplexer_1_out, reverse_bits_1_rev_out, reverse_bits_2_rev_out;

  reverse_bits reverse_bits_1 (.rev_in(rotate_in), .rev_out(reverse_bits_1_rev_out));
  Multiplexer #(.width(8)) multiplexer_1 (
    .in0(rotate_in), .in1(reverse_bits_1_rev_out), .out(multiplexer_1_out), .sel(direction));
  left_rotator left_rotator_1 (
    .rotate_in(multiplexer_1_out), .shift_amount(shift_amount), .rotate_out(left_rotator_1_rotate_out));
  reverse_bits reverse_bits_2 (.rev_in(left_rotator_1_rotate_out), .rev_out(reverse_bits_2_rev_out));
  Multiplexer #(.width(8)) multiplexer_2 (
    .in0(left_rotator_1_rotate_out), .in1(reverse_bits_2_rev_out), .out(rotate_out), .sel(direction));
endmodule

module shift_rotate (
  input  [7:0] data_in,
  input  [1:0] shift_mode,
  input  [2:0] shift_amount,
  output [7:0] data_out,
  output carry
);

  wire and_1_out, and_2_out, multiplexer_1_out, multiplexer_2_out, not_1_out;
  wire [7:0] barrel_rotator_1_rotate_out, barrel_shifter_1_shift_out;

  barrel_shifter barrel_shifter_1 (
    .shift_in(data_in), .direction(shift_mode[0]), .shift_amount(shift_amount),
    .shift_out(barrel_shifter_1_shift_out));
  barrel_rotator barrel_rotator_1 (
    .rotate_in(data_in), .direction(shift_mode[0]), .shift_amount(shift_amount),
    .rotate_out(barrel_rotator_1_rotate_out));
  Multiplexer #(.select(3)) multiplexer_1 (
    .in0(1'b0), .in1(data_in[0]), .in2(data_in[1]), .in3(data_in[2]), .in4(data_in[3]), .in5(data_in[4]),
    .in6(data_in[5]), .in7(data_in[6]), .out(multiplexer_1_out), .sel(shift_amount));
  Multiplexer #(.select(3)) multiplexer_2 (
    .in0(1'b0), .in1(data_in[7]), .in2(data_in[6]), .in3(data_in[5]), .in4(data_in[4]), .in5(data_in[3]),
    .in6(data_in[2]), .in7(data_in[1]), .out(multiplexer_2_out), .sel(shift_amount));
  Multiplexer #(.width(8)) multiplexer_3 (
    .in0(barrel_shifter_1_shift_out), .in1(barrel_rotator_1_rotate_out), .out(data_out), .sel(shift_mode[1]));
  not not_1 (not_1_out, shift_mode[0]);
  and and_1 (and_1_out, not_1_out, multiplexer_2_out);
  and and_2 (and_2_out, shift_mode[0], multiplexer_1_out);
  xor xor_1 (carry, and_1_out, and_2_out);
endmodule

module flag_updater (
  input  [7:0] alu_out,
  input  adder_carry_out,
  input  sub_en,
  output hasCarry,
  output isEven,
  output isZero,
  output isNegative
);

  xor xor_1 (hasCarry, adder_carry_out, sub_en);
  xnor even_parity_1 (isEven, alu_out[0], alu_out[1], alu_out[2], alu_out[3], alu_out[4], alu_out[5], alu_out[6], alu_out[7]);
  nor nor_1 (isZero, alu_out[0], alu_out[1], alu_out[2], alu_out[3], alu_out[4], alu_out[5], alu_out[6], alu_out[7]);
  and and_1 (isNegative, alu_out[7], sub_en);
endmodule
